// Logisim project Decoder final file.circ as structural Verilog: 1 circuit, main circuit main
module main (
  input  in_1
);

  wire and_1_out, clock_1_out, decoder_1_out0, decoder_1_out1, decoder_1_out2, decoder_1_out3,
       decoder_1_out4, decoder_1_out5, decoder_1_out6, decoder_1_out7, decoder_1_out8, decoder_1_out9,
       decoder_1_out10, decoder_1_out11, decoder_1_out12, decoder_1_out13, decoder_1_out14, decoder_1_out15,
       FF0_qn, FF1_qn, FF2_qn, FF3_qn, J3_out, JK1_out, JK2_out, K3_out, or_1_out, or_2_out, or_3_out,
       or_4_out, or_5_out, or_6_out, or_7_out;
  wire [3:0] FF0_q;

  Clock clock_1 (.out(clock_1_out));
  and JK1 (JK1_out, FF0_q[0], FF3_qn);
  and JK2 (JK2_out, FF0_q[0], FF0_q[1], FF3_qn);
  and K3 (K3_out, FF0_qn, FF1_qn, FF2_qn);
  and J3 (J3_out, and_1_out, FF3_qn);
  and and_1 (and_1_out, FF0_q[0], FF0_q[1], FF0_q[2]);
  J_K_Flip_Flop FF3 (.J(J3_out), .clk(clock_1_out), .K(K3_out), .Q(FF0_q[3]), .Qn(FF3_qn));  // open: preset, en, reset
  Decoder #(.select(4)) decoder_1 (
    .out0(decoder_1_out0), .out1(decoder_1_out1), .out2(decoder_1_out2), .out3(decoder_1_out3),
    .out4(decoder_1_out4), .out5(decoder_1_out5), .out6(decoder_1_out6), .out7(decoder_1_out7),
    .out8(decoder_1_out8), .out9(decoder_1_out9), .out10(decoder_1_out10), .out11(decoder_1_out11),
    .out12(decoder_1_out12), .out13(decoder_1_out13), .out14(decoder_1_out14), .out15(decoder_1_out15),
    .sel(FF0_q), .en(in_1));
  J_K_Flip_Flop FF2 (
    .J(JK2_out), .clk(clock_1_out), .K(JK2_out), .Q(FF0_q[2]), .Qn(FF2_qn));  // open: preset, en, reset
  J_K_Flip_Flop FF1 (
    .J(JK1_out), .clk(clock_1_out), .K(JK1_out), .Q(FF0_q[1]), .Qn(FF1_qn));  // open: preset, en, reset
  J_K_Flip_Flop FF0 (.J(FF3_qn), .clk(clock_1_out), .K(FF3_qn), .Q(FF0_q[0]), .Qn(FF0_qn));  // open: preset, en, reset
  or or_1 (or_1_out, decoder_1_out0, decoder_1_out7, decoder_1_out8);
  or or_2 (or_2_out, decoder_1_out0, decoder_1_out3, decoder_1_out5, decoder_1_out6);
  or or_3 (or_3_out, decoder_1_out0, decoder_1_out1, decoder_1_out2, decoder_1_out3, decoder_1_out5, decoder_1_out6, decoder_1_out7, decoder_1_out8);
  or or_4 (or_4_out, decoder_1_out1, decoder_1_out7, decoder_1_out8);
  or or_5 (or_5_out, decoder_1_out0, decoder_1_out1, decoder_1_out2, decoder_1_out7);
  or or_6 (or_6_out, decoder_1_out0, decoder_1_out1, decoder_1_out2, decoder_1_out6, decoder_1_out7, decoder_1_out8);
  or or_7 (or_7_out, decoder_1_out0, decoder_1_out1, decoder_1_out2, decoder_1_out4, decoder_1_out6, decoder_1_out7, decoder_1_out8);
  _7_Segment_Display u_7_segment_display_1 (
    .g(or_7_out), .f(or_6_out), .a(or_1_out), .b(or_2_out), .e(or_5_out), .d(or_4_out), .c(or_3_out));  // open: dp
endmodule
