// Logisim project MUX Final.circ as structural Verilog: 1 circuit, main circuit main
module main (
  input  _0,
  input  _1
);

  wire and_1_out, clock_1_out, FF0_q, FF0_qn, FF1_qn, FF2_qn, FF3_qn, J3_out, JK1_out, JK2_out, K3_out,
       multiplexer_1_out, multiplexer_2_out, multiplexer_3_out, multiplexer_4_out, multiplexer_5_out,
       multiplexer_6_out, multiplexer_7_out, not_1_out;
  wire [2:0] FF1_q;

  Clock clock_1 (.out(clock_1_out));
  and JK1 (JK1_out, FF0_q, FF3_qn);
  and JK2 (JK2_out, FF0_q, FF1_q[0], FF3_qn);
  and K3 (K3_out, FF0_qn, FF1_qn, FF2_qn);
  and J3 (J3_out, and_1_out, FF3_qn);
  not not_1 (not_1_out, FF0_q);
  and and_1 (and_1_out, FF0_q, FF1_q[0], FF1_q[1]);
  J_K_Flip_Flop FF3 (.J(J3_out), .clk(clock_1_out), .K(K3_out), .Q(FF1_q[2]), .Qn(FF3_qn));  // open: preset, en, reset
  Multiplexer #(.select(3)) multiplexer_1 (
    .in0(not_1_out), .in1(_0), .in2(_0), .in3(FF0_q), .in4(not_1_out), .in5(_0), .in6(_0), .in7(_0),
    .out(multiplexer_1_out), .sel(FF1_q));  // open: en
  Multiplexer #(.select(3)) multiplexer_2 (
    .in0(not_1_out), .in1(FF0_q), .in2(FF0_q), .in3(not_1_out), .in4(_0), .in5(_0), .in6(_0), .in7(_0),
    .out(multiplexer_2_out), .sel(FF1_q));  // open: en
  Multiplexer #(.select(3)) multiplexer_3 (
    .in0(_1), .in1(_1), .in2(FF0_q), .in3(_1), .in4(not_1_out), .in5(_0), .in6(_0), .in7(_0),
    .out(multiplexer_3_out), .sel(FF1_q));  // open: en
  Multiplexer #(.select(3)) multiplexer_4 (
    .in0(FF0_q), .in1(_0), .in2(_0), .in3(FF0_q), .in4(not_1_out), .in5(_0), .in6(_0), .in7(_0),
    .out(multiplexer_4_out), .sel(FF1_q));  // open: en
  Multiplexer #(.select(3)) multiplexer_5 (
    .in0(_1), .in1(not_1_out), .in2(_0), .in3(FF0_q), .in4(_0), .in5(_0), .in6(_0), .in7(_0),
    .out(multiplexer_5_out), .sel(FF1_q));  // open: en
  Multiplexer #(.select(3)) multiplexer_6 (
    .in0(_1), .in1(not_1_out), .in2(_0), .in3(_1), .in4(not_1_out), .in5(_0), .in6(_0), .in7(_0),
    .out(multiplexer_6_out), .sel(FF1_q));  // open: en
  Multiplexer #(.select(3)) multiplexer_7 (
    .in0(_1), .in1(not_1_out), .in2(not_1_out), .in3(_1), .in4(not_1_out), .in5(_0), .in6(_0), .in7(_0),
    .out(multiplexer_7_out), .sel(FF1_q));  // open: en
  J_K_Flip_Flop FF2 (
    .J(JK2_out), .clk(clock_1_out), .K(JK2_out), .Q(FF1_q[1]), .Qn(FF2_qn));  // open: preset, en, reset
  J_K_Flip_Flop FF1 (
    .J(JK1_out), .clk(clock_1_out), .K(JK1_out), .Q(FF1_q[0]), .Qn(FF1_qn));  // open: preset, en, reset
  _7_Segment_Display u_7_segment_display_1 (
    .g(multiplexer_7_out), .f(multiplexer_6_out), .a(multiplexer_1_out), .b(multiplexer_2_out),
    .e(multiplexer_5_out), .d(multiplexer_4_out), .c(multiplexer_3_out));  // open: dp
  J_K_Flip_Flop FF0 (.J(FF3_qn), .clk(clock_1_out), .K(FF3_qn), .Q(FF0_q), .Qn(FF0_qn));  // open: preset, en, reset
endmodule
