// Logisim project With Basic Gate final.circ as structural Verilog: 1 circuit, main circuit main
module main (
);

  wire and_1_out, and_2_out, and_3_out, and_4_out, and_5_out, and_6_out, and_7_out, and_8_out, and_9_out,
       and_10_out, and_11_out, and_12_out, and_13_out, and_14_out, and_15_out, and_16_out, and_17_out,
       and_18_out, and_19_out, and_20_out, and_21_out, and_22_out, and_23_out, and_24_out, clock_1_out,
       FF0_q, FF0_qn, FF1_q, FF1_qn, FF2_q, FF2_qn, FF3_q, FF3_qn, J3_out, JK1_out, JK2_out, K3_out,
       not_1_out, not_2_out, not_3_out, not_4_out, or_1_out, or_2_out, or_3_out, or_4_out, or_5_out,
       or_6_out, or_7_out;

  Clock clock_1 (.out(clock_1_out));
  not not_1 (not_1_out, FF3_q);
  and JK1 (JK1_out, FF0_q, FF3_qn);
  and JK2 (JK2_out, FF0_q, FF1_q, FF3_qn);
  and K3 (K3_out, FF0_qn, FF1_qn, FF2_qn);
  and J3 (J3_out, and_1_out, FF3_qn);
  not not_2 (not_2_out, FF2_q);
  and and_1 (and_1_out, FF0_q, FF1_q, FF2_q);
  J_K_Flip_Flop FF3 (.J(J3_out), .clk(clock_1_out), .K(K3_out), .Q(FF3_q), .Qn(FF3_qn));  // open: preset, en, reset
  not not_3 (not_3_out, FF0_q);
  not not_4 (not_4_out, FF1_q);
  J_K_Flip_Flop FF2 (.J(JK2_out), .clk(clock_1_out), .K(JK2_out), .Q(FF2_q), .Qn(FF2_qn));  // open: preset, en, reset
  and and_2 (and_2_out, not_2_out, not_4_out, not_3_out);
  and and_3 (and_3_out, not_1_out, FF2_q, FF1_q, FF0_q);
  and and_4 (and_4_out, not_1_out, not_2_out, not_4_out, not_3_out);
  and and_5 (and_5_out, not_1_out, not_2_out, FF1_q, FF0_q);
  and and_6 (and_6_out, not_1_out, FF2_q, not_4_out, FF0_q);
  and and_7 (and_7_out, not_1_out, FF2_q, FF1_q, not_3_out);
  and and_8 (and_8_out, not_1_out, FF0_q);
  and and_9 (and_9_out, not_1_out, FF1_q);
  and and_10 (and_10_out, not_2_out, not_4_out, not_3_out);
  and and_11 (and_11_out, not_1_out, not_2_out, not_4_out, FF0_q);
  and and_12 (and_12_out, not_1_out, FF2_q, FF1_q, FF0_q);
  and and_13 (and_13_out, FF3_q, not_2_out, not_4_out, not_3_out);
  and and_14 (and_14_out, not_1_out, not_2_out, not_4_out);
  and and_15 (and_15_out, not_1_out, not_2_out, not_3_out);
  and and_16 (and_16_out, not_1_out, FF2_q, FF1_q, FF0_q);
  and and_17 (and_17_out, not_1_out, not_2_out, not_4_out);
  and and_18 (and_18_out, not_1_out, not_2_out, not_3_out);
  and and_19 (and_19_out, not_2_out, not_4_out, not_3_out);
  and and_20 (and_20_out, not_1_out, FF2_q, FF1_q);
  and and_21 (and_21_out, not_1_out, not_3_out);
  and and_22 (and_22_out, not_1_out, not_2_out, not_4_out);
  and and_23 (and_23_out, not_2_out, not_4_out, not_3_out);
  and and_24 (and_24_out, not_1_out, FF2_q, FF1_q);
  J_K_Flip_Flop FF1 (.J(JK1_out), .clk(clock_1_out), .K(JK1_out), .Q(FF1_q), .Qn(FF1_qn));  // open: preset, en, reset
  or or_1 (or_1_out, and_2_out, and_3_out);
  or or_2 (or_2_out, and_4_out, and_5_out, and_6_out, and_7_out);
  or or_3 (or_3_out, and_8_out, and_9_out, and_10_out);
  or or_4 (or_4_out, and_11_out, and_12_out, and_13_out);
  or or_5 (or_5_out, and_14_out, and_15_out, and_16_out);
  or or_6 (or_6_out, and_17_out, and_18_out, and_19_out, and_20_out);
  or or_7 (or_7_out, and_21_out, and_22_out, and_23_out, and_24_out);
  J_K_Flip_Flop FF0 (.J(FF3_qn), .clk(clock_1_out), .K(FF3_qn), .Q(FF0_q), .Qn(FF0_qn));  // open: preset, en, reset
  _7_Segment_Display u_7_segment_display_1 (
    .g(or_7_out), .f(or_6_out), .a(or_1_out), .b(or_2_out), .e(or_5_out), .d(or_4_out), .c(or_3_out));  // open: dp
endmodule
