// Logisim project With Universal Gate final final trc.circ as structural Verilog: 1 circuit, main circuit main
module main (
);

  wire A_out, and_1_out, and_2_out, and_3_out, and_4_out, and_5_out, and_6_out, and_7_out, and_8_out,
       and_9_out, and_10_out, and_11_out, and_12_out, and_13_out, and_14_out, and_15_out, and_16_out,
       and_17_out, and_18_out, and_19_out, and_20_out, and_21_out, and_22_out, and_23_out, and_24_out,
       and_25_out, and_26_out, and_27_out, B_out, C_out, clock_1_out, D_out, FF0_q, FF0_qn, FF1_q, FF1_qn,
       FF2_q, FF2_qn, FF3_q, FF3_qn, J3_out, JK1_out, JK2_out, K3_out, nand_1_out, nand_2_out, nand_3_out,
       nand_4_out, nand_5_out, nand_6_out, nand_7_out, nand_8_out, nand_9_out, nand_10_out, nand_11_out,
       nand_12_out, nand_13_out, nand_14_out, nand_15_out, nand_16_out, not_1_out, not_2_out, not_3_out,
       not_4_out, not_5_out, not_6_out, not_7_out, not_8_out, not_9_out, not_10_out, not_11_out, not_12_out,
       not_13_out, not_14_out;

  Clock clock_1 (.out(clock_1_out));
  and JK1 (JK1_out, FF0_q, FF3_qn);
  and JK2 (JK2_out, FF0_q, FF1_q, FF3_qn);
  and K3 (K3_out, FF0_qn, FF1_qn, FF2_qn);
  and J3 (J3_out, and_1_out, FF3_qn);
  J_K_Flip_Flop FF3 (.J(J3_out), .clk(clock_1_out), .K(K3_out), .Q(FF3_q), .Qn(FF3_qn));  // open: preset, en, reset
  and and_1 (and_1_out, FF0_q, FF1_q, FF2_q);
  J_K_Flip_Flop FF2 (.J(JK2_out), .clk(clock_1_out), .K(JK2_out), .Q(FF2_q), .Qn(FF2_qn));  // open: preset, en, reset
  J_K_Flip_Flop FF1 (.J(JK1_out), .clk(clock_1_out), .K(JK1_out), .Q(FF1_q), .Qn(FF1_qn));  // open: preset, en, reset
  J_K_Flip_Flop FF0 (.J(FF3_qn), .clk(clock_1_out), .K(FF3_qn), .Q(FF0_q), .Qn(FF0_qn));  // open: preset, en, reset
  nand A (A_out, FF3_q, FF3_q);
  nand B (B_out, FF2_q, FF2_q);
  nand C (C_out, FF1_q, FF1_q);
  nand D (D_out, FF0_q, FF0_q);
  and and_2 (and_2_out, B_out, C_out, D_out);
  and and_3 (and_3_out, A_out, FF2_q, FF1_q);
  and and_4 (and_4_out, A_out, B_out, C_out);
  and and_5 (and_5_out, A_out, B_out, FF1_q);
  and and_6 (and_6_out, A_out, FF2_q, C_out);
  and and_7 (and_7_out, A_out, FF2_q, FF1_q);
  nand nand_1 (nand_1_out, A_out, FF0_q);
  nand nand_2 (nand_2_out, A_out, FF1_q);
  and and_8 (and_8_out, B_out, C_out, D_out);
  and and_9 (and_9_out, A_out, B_out, C_out);
  and and_10 (and_10_out, A_out, FF2_q, FF1_q);
  and and_11 (and_11_out, FF3_q, B_out, C_out);
  and and_12 (and_12_out, A_out, B_out, C_out);
  and and_13 (and_13_out, A_out, B_out, D_out);
  and and_14 (and_14_out, A_out, FF2_q, FF1_q);
  and and_15 (and_15_out, A_out, B_out, C_out);
  and and_16 (and_16_out, A_out, B_out, D_out);
  and and_17 (and_17_out, B_out, C_out, D_out);
  and and_18 (and_18_out, A_out, FF2_q, FF1_q);
  nand nand_3 (nand_3_out, A_out, D_out);
  and and_19 (and_19_out, A_out, B_out, C_out);
  and and_20 (and_20_out, B_out, C_out, D_out);
  and and_21 (and_21_out, A_out, FF2_q, FF1_q);
  not not_1 (not_1_out, and_2_out);
  not not_2 (not_2_out, and_8_out);
  not not_3 (not_3_out, and_12_out);
  not not_4 (not_4_out, and_13_out);
  not not_5 (not_5_out, and_15_out);
  not not_6 (not_6_out, and_16_out);
  not not_7 (not_7_out, and_17_out);
  not not_8 (not_8_out, and_18_out);
  not not_9 (not_9_out, and_19_out);
  not not_10 (not_10_out, and_20_out);
  not not_11 (not_11_out, and_21_out);
  and and_22 (and_22_out, nand_1_out, nand_2_out, not_2_out);
  and and_23 (and_23_out, not_5_out, not_6_out, not_7_out);
  and and_24 (and_24_out, nand_3_out, not_9_out, not_10_out);
  nand nand_4 (nand_4_out, and_3_out, FF0_q);
  nand nand_5 (nand_5_out, and_4_out, D_out);
  nand nand_6 (nand_6_out, and_5_out, FF0_q);
  nand nand_7 (nand_7_out, and_6_out, FF0_q);
  nand nand_8 (nand_8_out, and_7_out, D_out);
  not not_12 (not_12_out, and_22_out);
  nand nand_9 (nand_9_out, and_9_out, FF0_q);
  nand nand_10 (nand_10_out, and_10_out, FF0_q);
  nand nand_11 (nand_11_out, and_11_out, D_out);
  nand nand_12 (nand_12_out, and_14_out, FF0_q);
  nand nand_13 (nand_13_out, not_1_out, nand_4_out);
  and and_25 (and_25_out, nand_5_out, nand_6_out, nand_7_out);
  and and_26 (and_26_out, nand_9_out, nand_10_out, nand_11_out);
  and and_27 (and_27_out, not_3_out, not_4_out, nand_12_out);
  nand nand_14 (nand_14_out, and_23_out, not_8_out);
  nand nand_15 (nand_15_out, and_24_out, not_11_out);
  nand nand_16 (nand_16_out, and_25_out, nand_8_out);
  not not_13 (not_13_out, and_26_out);
  not not_14 (not_14_out, and_27_out);
  _7_Segment_Display u_7_segment_display_1 (
    .g(nand_15_out), .f(nand_14_out), .a(nand_13_out), .b(nand_16_out), .e(not_14_out), .d(not_13_out),
    .c(not_12_out));  // open: dp
endmodule
